# Fritzing sketch 7-Segment-Ard (saved by Fritzing 0.9.2b)
breadboards: 1

parts:
  DI1 = 7-Segment LED Display [package=THT]
  U2 = TRANSISTOR_NPN_2 [package=to-92]
  U3 = TRANSISTOR_NPN_2 [package=to-92]
  U4 = TRANSISTOR_NPN_2 [package=to-92]
  U5 = TRANSISTOR_NPN_2 [package=to-92]
  U6 = TRANSISTOR_NPN_2 [package=to-92]
  U7 = TRANSISTOR_NPN_2 [package=to-92]
  U8 = TRANSISTOR_NPN_2 [package=to-92]
  U9 = TRANSISTOR_NPN_2 [package=to-92]
  Part1 = Arduino Uno (Rev3)

nets:
  N1: DI1.cathodeE, U5.E
  N2: DI1.cathodeD, U4.E
  N3: DI1.cathodeC, U2.E
  N4: DI1.cathodeDP, U3.E
  N5: DI1.cathodeB, U9.E
  N6: DI1.cathodeA, U8.E
  N7: DI1.commAnode, Part1.3V3
  N8: DI1.cathodeF, U7.E
  N9: DI1.cathodeG, U6.E
  N10: U2.C, U3.C, U4.C, U5.C, U6.C, U7.C, U8.C, U9.C, Part1.GND
  N11: U2.B, Part1.D4
  N12: U3.B, Part1.D5_PWM
  N13: U4.B, Part1.D3_PWM
  N14: U5.B, Part1.D2
  N15: U6.B, Part1.D9_PWM
  N16: U7.B, Part1.D8
  N17: U8.B, Part1.D7
  N18: U9.B, Part1.D6_PWM
