# Fritzing sketch Temp with LED (saved by Fritzing 0.9.2b)
breadboards: 1

parts:
  DI1 = 7-Segment LED Display [package=THT]
  R1 = Resistor [tolerance=±5% resistance=150 package=THT]
  U1 = 74HC595 [package="DIP16 [THT]"]
  Part1 = Arduino Uno (Rev3)
  NOT_TMP36_DHT11_SENSOR = TMP36 [package=to-92-kit]

nets:
  N1: DI1.cathodeE, U1.Q4
  N2: DI1.cathodeD, U1.Q5
  N3: DI1.cathodeC, U1.Q6
  N4: DI1.cathodeDP, U1.Q7
  N5: DI1.cathodeB, U1.Q0
  N6: DI1.cathodeA, U1.Q1
  N7: DI1.commAnode, R1.Pin_0
  N8: DI1.cathodeF, U1.Q2
  N9: DI1.cathodeG, U1.Q3
  GND: R1.Pin_1, U1.GND, U1.OE, Part1.GND, NOT_TMP36_DHT11_SENSOR.GND
  VCC: U1.MR, U1.VCC, Part1.D2, Part1.5V, NOT_TMP36_DHT11_SENSOR.VCC, NOT_TMP36_DHT11_SENSOR.VOUT
  N10: U1.SH_CP, Part1.D10_PWM/SS
  N11: U1.ST_CP, Part1.D8
  N12: U1.DS, Part1.D6_PWM
